// Logisim project pattern_machine.circ as structural Verilog: 1 circuit, main circuit main
module main (
);

  wire and_1_out, clk, S1, S2, S3, S4;
  wire [0:0] pull_resistor_1_node;
  wire [3:0] pla_1_out;

  // Switch switch_1: pin names not known; wires that end beside it: 1'b1
  Pull_Resistor pull_resistor_1 (.node(pull_resistor_1_node[0]));
  Button button_1 (.out(clk));
  PLA #(.in_width(5), .out_width(4), .\table ("00000 0001\n00001 0000\n00010 0010\n00011 0000\n00100 0010\n00101 0011\n00110 0001\n00111 0100\n01000 0001\n01001 0101\n01010 0110\n01011 0000\n01100 0010\n01101 0111\n01110 0001\n01111 1000\n10000 1001\n10001 0000\n10010 0010\n10011 1010\n10100 0001\n10101 0000")) pla_1 (
    .in({S4, S3, S2, S1, pull_resistor_1_node[0]}), .out(pla_1_out));
  D_Flip_Flop d_ff_1 (.D(pla_1_out[0]), .clk(clk), .Q(S1));  // open: Qn, preset, reset
  D_Flip_Flop d_ff_2 (.D(pla_1_out[1]), .clk(clk), .Q(S2));  // open: Qn, preset, reset
  D_Flip_Flop d_ff_3 (.D(pla_1_out[2]), .clk(clk), .Q(S3));  // open: Qn, preset, reset
  D_Flip_Flop d_ff_4 (.D(pla_1_out[3]), .clk(clk), .Q(S4));  // open: Qn, preset, reset
  and and_1 (and_1_out, ~S1, S2, ~S3, S4);  // AND_Gate
  LED led_1 (.in(and_1_out));
endmodule
