// Logisim project vending_machine.circ as structural Verilog: 1 circuit, main circuit main
module main (
);

  wire clk, S1, S2, S3, S4;
  wire [1:0] pla_2_out;
  wire [3:0] pla_1_out;
  wire [8:4] dipswitch_1_p1;

  // DipSwitch #(.number(3)) dipswitch_1: pin names not known; wires that end beside it: dipswitch_1_p1[4], dipswitch_1_p1[5]
  // DipSwitch #(.number(2)) dipswitch_2: pin names not known; wires that end beside it: dipswitch_1_p1[6], dipswitch_1_p1[7], dipswitch_1_p1[8]
  Button button_1 (.out(clk));
  PLA #(.in_width(9), .out_width(4), .\table ("xx0000000 0001\nxx1000000 0010\nxx0100000 0100\nxx1100000 0101\nxx0010000 1000\nxx1010000 1011\nxx1110000 0000\n00xxx1000 0001\n10xxx1000 1110\n01xxx1000 1111\n11xxx1000 1111\n00xxx0100 0010\n10xxx0100 0001\n01xxx0100 1111\n11xxx0100 1111\n00xxx1100 0011\n10xxx1100 0010\n01xxx1100 1111\n11xxx1100 1111\n00xxx0010 0100\n10xxx0010 0011\n01xxx0010 1110\n11xxx0010 1111\n00xxx1010 0101\n10xxx1010 0100\n01xxx1010 0001\n11xxx1010 1111\n00xxx0110 0110\n10xxx0110 0101\n01xxx0110 1111\n11xxx0110 1111\n00xxx1110 0111\n10xxx1110 0110\n01xxx1110 0011\n11xxx1110 1111\n00xxx0001 1000\n10xxx0001 0111\n01xxx0001 0100\n11xxx0001 1111\n00xxx1001 1001\n10xxx1001 1000\n01xxx1001 0101\n11xxx1001 1111\n00xxx0101 1010\n10xxx0101 1001\n01xxx0101 0110\n11xxx0101 1110\n00xxx1101 1011\n10xxx1101 1010\n01xxx1101 0111\n11xxx1101 0001\nxxxxx0111 0000\nxxxxx1111 0000")) pla_1 (
    .in({dipswitch_1_p1, S1, S2, S3, S4}), .out(pla_1_out));
  D_Flip_Flop d_ff_1 (.D(pla_1_out[0]), .clk(clk), .Q(S1));  // open: Qn, preset, reset
  D_Flip_Flop d_ff_2 (.D(pla_1_out[1]), .clk(clk), .Q(S2));  // open: Qn, preset, reset
  D_Flip_Flop d_ff_3 (.D(pla_1_out[2]), .clk(clk), .Q(S3));  // open: Qn, preset, reset
  D_Flip_Flop d_ff_4 (.D(pla_1_out[3]), .clk(clk), .Q(S4));  // open: Qn, preset, reset
  PLA #(.in_width(4), .\table ("1110 10\n1111 11\nxxxx 00")) pla_2 (.in({S4, S3, S2, S1}), .out(pla_2_out));
  LED led_1 (.in(pla_2_out[0]));
  LED led_2 (.in(pla_2_out[1]));
endmodule
